// Logisim project BCD Adder.circ as structural Verilog: 2 circuits, main circuit Full Adder
module Full_Adder (
  input  A,
  input  B,
  input  C,
  output S,
  output C_2
);

  wire and_1_out, and_2_out, xor_1_out;

  xor xor_1 (xor_1_out, A, B);
  and and_1 (and_1_out, A, B);
  xor xor_2 (S, xor_1_out, C);
  and and_2 (and_2_out, xor_1_out, C);
  or or_1 (C_2, and_2_out, and_1_out);
endmodule

module main_2 (
  input  A4,
  input  B4,
  input  A3,
  input  B3,
  input  A2,
  input  B2,
  input  A1,
  input  B1,
  input  Cin,
  input  in_10,
  input  in_11,
  output out_12,
  output out_13,
  output out_14,
  output out_15
);

  wire and_1_out, and_2_out, full_adder_1_c_2, full_adder_1_s, full_adder_3_c_2, full_adder_3_s,
       full_adder_4_c_2, full_adder_5_c_2, full_adder_5_s, full_adder_6_c_2, full_adder_7_c_2,
       full_adder_7_s, full_adder_8_c_2, or_1_out, or_2_out;

  or or_1 (or_1_out, full_adder_1_c_2, or_2_out);
  or or_2 (or_2_out, and_1_out, and_2_out);
  Full_Adder full_adder_1 (.A(B4), .B(A4), .C(full_adder_3_c_2), .S(full_adder_1_s), .C_2(full_adder_1_c_2));
  and and_1 (and_1_out, full_adder_3_s, full_adder_1_s);
  and and_2 (and_2_out, full_adder_1_s, full_adder_5_s);
  Full_Adder full_adder_2 (.A(full_adder_1_s), .B(in_11), .C(full_adder_4_c_2), .S(out_13));  // open: C_2
  Full_Adder full_adder_3 (.A(B3), .B(A3), .C(full_adder_5_c_2), .S(full_adder_3_s), .C_2(full_adder_3_c_2));
  Full_Adder full_adder_4 (.A(full_adder_3_s), .B(or_1_out), .C(full_adder_6_c_2), .S(out_14), .C_2(full_adder_4_c_2));
  Full_Adder full_adder_5 (.A(B2), .B(A2), .C(full_adder_7_c_2), .S(full_adder_5_s), .C_2(full_adder_5_c_2));
  Full_Adder full_adder_6 (.A(full_adder_5_s), .B(or_1_out), .C(full_adder_8_c_2), .S(out_15), .C_2(full_adder_6_c_2));
  Full_Adder full_adder_7 (.A(B1), .B(A1), .C(Cin), .S(full_adder_7_s), .C_2(full_adder_7_c_2));
  Full_Adder full_adder_8 (.A(full_adder_7_s), .B(in_11), .C(in_10), .S(out_12), .C_2(full_adder_8_c_2));

  // Notes on the sheet:
  //   2211577042
  //   Mohammed Arif Mainuddin
  //   S4
  //   S3
  //   S2
  //   S1
endmodule
