// Logisim project Binary-Adder-Subtractor.circ as structural Verilog: 2 circuits, main circuit Full Adder
module Full_Adder (
  input  A,
  input  B,
  input  C,
  output S,
  output C_2
);

  wire and_1_out, and_2_out, xor_1_out;

  xor xor_1 (xor_1_out, A, B);
  and and_1 (and_1_out, A, B);
  xor xor_2 (S, xor_1_out, C);
  and and_2 (and_2_out, xor_1_out, C);
  or or_1 (C_2, and_2_out, and_1_out);
endmodule

module main_2 (
  input  A4,
  input  B4,
  input  A3,
  input  B3,
  input  A2,
  input  B2,
  input  A1,
  input  B1,
  input  Mode,
  output out_10,
  output S4,
  output S3,
  output out_13,
  output out_14
);

  wire full_adder_2_c_2, full_adder_3_c_2, full_adder_4_c_2, xor_1_out, xor_2_out, xor_3_out, xor_4_out;

  xor xor_1 (xor_1_out, Mode, B4);
  Full_Adder full_adder_1 (.A(xor_1_out), .B(A4), .C(full_adder_2_c_2), .S(S4), .C_2(out_10));
  xor xor_2 (xor_2_out, Mode, B3);
  Full_Adder full_adder_2 (.A(xor_2_out), .B(A3), .C(full_adder_3_c_2), .S(S3), .C_2(full_adder_2_c_2));
  xor xor_3 (xor_3_out, Mode, B2);
  Full_Adder full_adder_3 (.A(xor_3_out), .B(A2), .C(full_adder_4_c_2), .S(out_13), .C_2(full_adder_3_c_2));
  xor xor_4 (xor_4_out, Mode, B1);
  Full_Adder full_adder_4 (.A(xor_4_out), .B(A1), .C(Mode), .S(out_14), .C_2(full_adder_4_c_2));

  // Notes on the sheet:
  //   2211577042
  //   Mohammed Arif Mainuddin
  //   Carry Out
  //   S2
  //   S1
endmodule
