// Logisim project Lab - 7 _ D Flip Flop.circ as structural Verilog: 1 circuit, main circuit main
module main (
  input  in_1,
  input  in_2
);

  wire button_1_out, button_2_out, clock_1_out, clock_2_out, d_ff_1_q, d_ff_2_q, d_ff_3_q, d_ff_4_q,
       d_ff_5_q, d_ff_6_q, d_ff_7_q, d_ff_8_q;

  Clock clock_1 (.out(clock_1_out));
  Button button_1 (.out(button_1_out));
  Clock clock_2 (.out(clock_2_out));
  Button button_2 (.out(button_2_out));
  LED led_1 (.in(d_ff_1_q));
  D_Flip_Flop d_ff_1 (.clk(clock_1_out), .D(in_1), .Q(d_ff_1_q), .reset(button_1_out));  // open: Qn, preset, en
  D_Flip_Flop d_ff_2 (.clk(clock_2_out), .D(in_2), .Q(d_ff_2_q), .reset(button_2_out));  // open: Qn, preset, en
  LED led_2 (.in(d_ff_3_q));
  D_Flip_Flop d_ff_3 (.clk(clock_1_out), .D(d_ff_1_q), .Q(d_ff_3_q), .reset(button_1_out));  // open: Qn, preset, en
  D_Flip_Flop d_ff_4 (.clk(clock_2_out), .D(d_ff_2_q), .Q(d_ff_4_q), .reset(button_2_out));  // open: Qn, preset, en
  LED led_3 (.in(d_ff_5_q));
  D_Flip_Flop d_ff_5 (.clk(clock_1_out), .D(d_ff_3_q), .Q(d_ff_5_q), .reset(button_1_out));  // open: Qn, preset, en
  D_Flip_Flop d_ff_6 (.clk(clock_2_out), .D(d_ff_4_q), .Q(d_ff_6_q), .reset(button_2_out));  // open: Qn, preset, en
  D_Flip_Flop d_ff_7 (.clk(clock_1_out), .D(d_ff_5_q), .Q(d_ff_7_q), .reset(button_1_out));  // open: Qn, preset, en
  LED led_4 (.in(d_ff_7_q));
  D_Flip_Flop d_ff_8 (.clk(clock_2_out), .D(d_ff_6_q), .Q(d_ff_8_q), .reset(button_2_out));  // open: Qn, preset, en
  LED led_5 (.in(d_ff_8_q));

  // Notes on the sheet:
  //   SIPO : 
  //   SISO : 
  //   ID : 2211577042
  //   Name : Mohammed Arif Mainuddin
endmodule
