// Logisim project Ripple-Through-Carry Adder.circ as structural Verilog: 2 circuits, main circuit Full Adder
module Full_Adder (
  input  A,
  input  B,
  input  C,
  output S,
  output C_2
);

  wire and_1_out, and_2_out, xor_1_out;

  xor xor_1 (xor_1_out, A, B);
  and and_1 (and_1_out, A, B);
  xor xor_2 (S, xor_1_out, C);
  and and_2 (and_2_out, xor_1_out, C);
  or or_1 (C_2, and_2_out, and_1_out);
endmodule

module main_2 (
  input  A4,
  input  B4,
  input  A3,
  input  B3,
  input  A2,
  input  B2,
  input  A1,
  input  B1,
  input  Carry_In,
  output out_10,
  output S4,
  output S3,
  output out_13,
  output out_14
);

  wire full_adder_2_c_2, full_adder_3_c_2, full_adder_4_c_2;

  Full_Adder full_adder_1 (.A(B4), .B(A4), .C(full_adder_2_c_2), .S(S4), .C_2(out_10));
  Full_Adder full_adder_2 (.A(B3), .B(A3), .C(full_adder_3_c_2), .S(S3), .C_2(full_adder_2_c_2));
  Full_Adder full_adder_3 (.A(B2), .B(A2), .C(full_adder_4_c_2), .S(out_13), .C_2(full_adder_3_c_2));
  Full_Adder full_adder_4 (.A(B1), .B(A1), .C(Carry_In), .S(out_14), .C_2(full_adder_4_c_2));

  // Notes on the sheet:
  //   2211577042
  //   Mohammed Arif Mainuddin
  //   Carry Out
  //   S2
  //   S1
endmodule
