// Logisim project WorkStation_07 (1).circ as structural Verilog: 6 circuits, main circuit main
module main (
  input  A,
  input  B,
  input  C,
  input  A_2,
  input  B_2,
  input  C_2,
  input  A_3,
  input  B_3,
  input  C_3,
  input  A_4,
  input  B_4,
  input  C_4,
  input  A_5,
  input  B_5,
  input  C_5
);

  wire NAND_a_2, NAND_b_2, NAND_c_2, NAND_d, NAND_e, NAND_f, NAND_g, Nor_out_4, Nor_out_5, Nor_out_6,
       Nor_out_7, Nor_out_8, Nor_out_9, Nor_out_10, Optimized_a_2, Optimized_b_2, Optimized_c_2, Optimized_d,
       Optimized_e, Optimized_f, Optimized_g, POS_a_2, POS_b_2, POS_c_2, POS_d, POS_e, POS_f, POS_g, SOP_a_2,
       SOP_b_2, SOP_c_2, SOP_d, SOP_e, SOP_f, SOP_f_2;

  Nand NAND (
    .A(A), .B(B), .C(C), .a_2(NAND_a_2), .b_2(NAND_b_2), .c_2(NAND_c_2), .d(NAND_d), .e(NAND_e), .f(NAND_f),
    .g(NAND_g));
  Nor Nor (
    .out_8(Nor_out_8), .out_9(Nor_out_9), .A(A_3), .B(B_3), .C(C_3), .out_10(Nor_out_10), .out_7(Nor_out_7),
    .out_6(Nor_out_6), .out_5(Nor_out_5), .out_4(Nor_out_4));
  Optimized Optimized (
    .A(A_5), .B(B_5), .C(C_5), .a_2(Optimized_a_2), .b_2(Optimized_b_2), .c_2(Optimized_c_2),
    .d(Optimized_d), .e(Optimized_e), .f(Optimized_f), .g(Optimized_g));
  _7_Segment_Display u_7_segment_display_1 (
    .g(NAND_g), .f(NAND_f), .a(NAND_a_2), .b(NAND_b_2), .e(NAND_e), .d(NAND_d), .c(NAND_c_2));  // open: dp
  _7_Segment_Display u_7_segment_display_2 (
    .g(Nor_out_10), .f(Nor_out_9), .a(Nor_out_4), .b(Nor_out_5), .e(Nor_out_8), .d(Nor_out_7), .c(Nor_out_6));  // open: dp
  _7_Segment_Display u_7_segment_display_3 (
    .g(Optimized_g), .f(Optimized_f), .a(Optimized_a_2), .b(Optimized_b_2), .e(Optimized_e), .d(Optimized_d),
    .c(Optimized_c_2));  // open: dp
  SOP SOP (
    .A(A_2), .B(B_2), .C(C_2), .a_2(SOP_a_2), .b_2(SOP_b_2), .c_2(SOP_c_2), .d(SOP_d), .e(SOP_e), .f(SOP_f),
    .f_2(SOP_f_2));
  POS POS (
    .A(A_4), .B(B_4), .C(C_4), .a_2(POS_a_2), .b_2(POS_b_2), .c_2(POS_c_2), .d(POS_d), .e(POS_e), .f(POS_f),
    .g(POS_g));
  _7_Segment_Display u_7_segment_display_4 (
    .g(SOP_f_2), .f(SOP_f), .a(SOP_a_2), .b(SOP_b_2), .e(SOP_e), .d(SOP_d), .c(SOP_c_2));  // open: dp
  _7_Segment_Display u_7_segment_display_5 (
    .g(POS_g), .f(POS_f), .a(POS_a_2), .b(POS_b_2), .e(POS_e), .d(POS_d), .c(POS_c_2));  // open: dp
endmodule

module Nand (
  input  A,
  input  B,
  input  C,
  output a_2,
  output b_2,
  output c_2,
  output d,
  output e,
  output f,
  output g
);

  wire nand_1_out, nand_2_out, nand_3_out, nand_4_out, nand_5_out, nand_6_out, nand_7_out, nand_8_out,
       nand_9_out, nand_10_out, nand_11_out, nand_12_out, nand_13_out, nand_14_out, nand_15_out, nand_16_out,
       nand_17_out, nand_18_out, nand_19_out, nand_20_out, nand_21_out, nand_22_out, nand_23_out,
       nand_24_out, nand_25_out, nand_26_out, nand_27_out, nand_28_out, nand_29_out, nand_30_out,
       nand_31_out, nand_32_out, nand_33_out, nand_34_out, nand_35_out, nand_36_out, nand_38_out,
       nand_39_out, nand_40_out, nand_41_out, nand_42_out, nand_43_out, nand_44_out, nand_45_out,
       nand_46_out, nand_47_out, nand_48_out, nand_49_out, nand_50_out, nand_51_out, nand_52_out,
       nand_53_out, nand_54_out, nand_55_out, nand_56_out, nand_57_out, nand_58_out, nand_59_out,
       nand_60_out, nand_61_out, nand_62_out, nand_63_out, nand_64_out, nand_65_out, nand_69_out,
       nand_70_out, nand_71_out, nand_73_out, nand_74_out, nand_75_out, nand_76_out;

  nand nand_1 (nand_1_out, A, A);
  nand nand_2 (nand_2_out, B, B);
  nand nand_3 (nand_3_out, C, C);
  nand nand_4 (nand_4_out, A, A);
  nand nand_5 (nand_5_out, B, B);
  nand nand_6 (nand_6_out, A, A);
  nand nand_7 (nand_7_out, B, B);
  nand nand_8 (nand_8_out, B, B);
  nand nand_9 (nand_9_out, A, A);
  nand nand_10 (nand_10_out, B, B);
  nand nand_11 (nand_11_out, B, B);
  nand nand_12 (nand_12_out, C, C);
  nand nand_13 (nand_13_out, A, A);
  nand nand_14 (nand_14_out, A, A);
  nand nand_15 (nand_15_out, B, B);
  nand nand_16 (nand_16_out, A, A);
  nand nand_17 (nand_17_out, B, B);
  nand nand_18 (nand_18_out, A, A);
  nand nand_19 (nand_19_out, A, A);
  nand nand_20 (nand_20_out, B, B);
  nand nand_21 (nand_21_out, B, B);
  nand nand_22 (nand_22_out, C, C);
  nand nand_23 (nand_23_out, nand_1_out, nand_2_out);
  nand nand_24 (nand_24_out, A, nand_3_out);
  nand nand_25 (nand_25_out, nand_4_out, nand_5_out);
  nand nand_26 (nand_26_out, nand_6_out, nand_7_out);
  nand nand_27 (nand_27_out, nand_8_out, C);
  nand nand_28 (nand_28_out, nand_9_out, nand_10_out);
  nand nand_29 (nand_29_out, nand_11_out, nand_12_out);
  nand nand_30 (nand_30_out, nand_13_out, C);
  nand nand_31 (nand_31_out, nand_14_out, B);
  nand nand_32 (nand_32_out, A, nand_15_out);
  nand nand_33 (nand_33_out, nand_16_out, nand_17_out);
  nand nand_34 (nand_34_out, nand_18_out, B);
  nand nand_35 (nand_35_out, nand_19_out, nand_20_out);
  nand nand_36 (nand_36_out, nand_21_out, nand_22_out);
  nand nand_37 (a_2, nand_23_out, nand_24_out);
  nand nand_38 (nand_38_out, nand_25_out, nand_25_out);
  nand nand_39 (nand_39_out, C, C);
  nand nand_40 (nand_40_out, nand_26_out, nand_27_out);
  nand nand_41 (nand_41_out, nand_28_out, nand_29_out);
  nand nand_42 (nand_42_out, A, A);
  nand nand_43 (nand_43_out, nand_30_out, nand_31_out);
  nand nand_44 (nand_44_out, nand_32_out, nand_32_out);
  nand nand_45 (nand_45_out, C, C);
  nand nand_46 (nand_46_out, nand_33_out, nand_33_out);
  nand nand_47 (nand_47_out, nand_34_out, nand_34_out);
  nand nand_48 (nand_48_out, C, C);
  nand nand_49 (nand_49_out, B, B);
  nand nand_50 (nand_50_out, nand_35_out, nand_36_out);
  nand nand_51 (nand_51_out, A, A);
  nand nand_52 (nand_52_out, nand_38_out, nand_39_out);
  nand nand_53 (nand_53_out, A, C);
  nand nand_54 (nand_54_out, nand_40_out, nand_40_out);
  nand nand_55 (nand_55_out, A, B);
  nand nand_56 (nand_56_out, nand_41_out, nand_41_out);
  nand nand_57 (nand_57_out, nand_42_out, C);
  nand nand_58 (nand_58_out, nand_43_out, nand_43_out);
  nand nand_59 (nand_59_out, nand_44_out, nand_45_out);
  nand nand_60 (nand_60_out, nand_46_out, C);
  nand nand_61 (nand_61_out, nand_47_out, nand_48_out);
  nand nand_62 (nand_62_out, A, nand_49_out);
  nand nand_63 (nand_63_out, nand_50_out, nand_50_out);
  nand nand_64 (nand_64_out, nand_51_out, C);
  nand nand_65 (nand_65_out, nand_52_out, nand_53_out);
  nand nand_66 (c_2, nand_54_out, nand_55_out);
  nand nand_67 (d, nand_56_out, nand_57_out);
  nand nand_68 (e, nand_58_out, nand_59_out);
  nand nand_69 (nand_69_out, nand_60_out, nand_61_out);
  nand nand_70 (nand_70_out, nand_62_out, nand_62_out);
  nand nand_71 (nand_71_out, C, C);
  nand nand_72 (g, nand_63_out, nand_64_out);
  nand nand_73 (nand_73_out, nand_65_out, nand_65_out);
  nand nand_74 (nand_74_out, A, B);
  nand nand_75 (nand_75_out, nand_69_out, nand_69_out);
  nand nand_76 (nand_76_out, nand_70_out, nand_71_out);
  nand nand_77 (b_2, nand_73_out, nand_74_out);
  nand nand_78 (f, nand_75_out, nand_76_out);
  _7_Segment_Display u_7_segment_display_1 (.g(g), .f(f), .a(a_2), .b(b_2), .e(e), .d(d), .c(c_2));  // open: dp
endmodule

module Nor (
  input  A,
  input  B,
  input  C,
  output out_4,
  output out_5,
  output out_6,
  output out_7,
  output out_8,
  output out_9,
  output out_10
);

  wire nor_1_out, nor_2_out, nor_3_out, nor_4_out, nor_5_out, nor_6_out, nor_7_out, nor_8_out, nor_9_out,
       nor_10_out, nor_11_out, nor_12_out, nor_13_out, nor_14_out, nor_15_out, nor_16_out, nor_17_out,
       nor_18_out, nor_19_out, nor_20_out, nor_21_out, nor_22_out, nor_23_out, nor_24_out, nor_25_out,
       nor_26_out, nor_27_out, nor_28_out, nor_29_out, nor_30_out, nor_31_out, nor_33_out, nor_34_out,
       nor_35_out, nor_36_out, nor_38_out, nor_39_out, nor_40_out, nor_41_out, nor_42_out, nor_43_out,
       nor_45_out, nor_47_out, nor_48_out, nor_50_out, nor_52_out;

  nor nor_1 (nor_1_out, A, A);
  nor nor_2 (nor_2_out, B, B);
  nor nor_3 (nor_3_out, C, C);
  nor nor_4 (nor_4_out, A, B);
  nor nor_5 (nor_5_out, nor_1_out, C);
  nor nor_6 (nor_6_out, A, B);
  nor nor_7 (nor_7_out, nor_1_out, nor_3_out);
  nor nor_8 (nor_8_out, nor_1_out, nor_2_out);
  nor nor_9 (nor_9_out, A, B);
  nor nor_10 (nor_10_out, B, nor_3_out);
  nor nor_11 (nor_11_out, nor_1_out, nor_2_out);
  nor nor_12 (nor_12_out, B, C);
  nor nor_13 (nor_13_out, A, nor_3_out);
  nor nor_14 (nor_14_out, A, nor_3_out);
  nor nor_15 (nor_15_out, A, nor_2_out);
  nor nor_16 (nor_16_out, nor_1_out, B);
  nor nor_17 (nor_17_out, A, B);
  nor nor_18 (nor_18_out, A, nor_2_out);
  nor nor_19 (nor_19_out, nor_1_out, B);
  nor nor_20 (nor_20_out, B, C);
  nor nor_21 (nor_21_out, A, nor_3_out);
  nor nor_22 (nor_22_out, nor_4_out, nor_5_out);
  nor nor_23 (nor_23_out, nor_6_out, nor_6_out);
  nor nor_24 (nor_24_out, nor_9_out, nor_10_out);
  nor nor_25 (nor_25_out, nor_12_out, nor_13_out);
  nor nor_26 (nor_26_out, nor_14_out, nor_15_out);
  nor nor_27 (nor_27_out, nor_16_out, nor_16_out);
  nor nor_28 (nor_28_out, nor_17_out, nor_17_out);
  nor nor_29 (nor_29_out, nor_18_out, nor_18_out);
  nor nor_30 (nor_30_out, nor_19_out, nor_19_out);
  nor nor_31 (nor_31_out, nor_20_out, nor_21_out);
  nor nor_32 (out_4, nor_22_out, nor_22_out);
  nor nor_33 (nor_33_out, nor_23_out, C);
  nor nor_34 (nor_34_out, nor_33_out, nor_7_out);
  nor nor_35 (nor_35_out, nor_24_out, nor_24_out);
  nor nor_36 (nor_36_out, nor_35_out, nor_11_out);
  nor nor_37 (out_7, nor_25_out, nor_25_out);
  nor nor_38 (nor_38_out, nor_26_out, nor_26_out);
  nor nor_39 (nor_39_out, nor_27_out, C);
  nor nor_40 (nor_40_out, nor_28_out, nor_3_out);
  nor nor_41 (nor_41_out, nor_40_out, nor_42_out);
  nor nor_42 (nor_42_out, nor_29_out, C);
  nor nor_43 (nor_43_out, nor_30_out, C);
  nor nor_44 (out_10, nor_31_out, nor_31_out);
  nor nor_45 (nor_45_out, nor_34_out, nor_34_out);
  nor nor_46 (out_6, nor_36_out, nor_36_out);
  nor nor_47 (nor_47_out, nor_38_out, nor_39_out);
  nor nor_48 (nor_48_out, nor_41_out, nor_41_out);
  nor nor_49 (out_5, nor_50_out, nor_50_out);
  nor nor_50 (nor_50_out, nor_45_out, nor_8_out);
  nor nor_51 (out_8, nor_47_out, nor_47_out);
  nor nor_52 (nor_52_out, nor_48_out, nor_43_out);
  nor nor_53 (out_9, nor_52_out, nor_52_out);
  _7_Segment_Display u_7_segment_display_1 (
    .g(out_10), .f(out_9), .a(out_4), .b(out_5), .e(out_8), .d(out_7), .c(out_6));  // open: dp
endmodule

module Optimized (
  input  A,
  input  B,
  input  C,
  output a_2,
  output b_2,
  output c_2,
  output d,
  output e,
  output f,
  output g
);

  wire and_1_out, and_2_out, and_3_out, and_4_out, and_5_out, and_6_out, and_7_out, and_8_out, and_9_out,
       and_10_out, and_11_out, and_12_out, and_13_out, and_14_out, and_15_out, and_16_out, and_17_out,
       and_18_out, and_19_out, and_20_out, and_21_out, and_22_out, and_23_out, and_24_out, and_25_out,
       not_1_out, not_2_out, not_3_out, not_4_out, not_5_out, not_6_out, not_7_out, not_8_out, not_9_out,
       not_10_out, not_11_out, not_12_out, not_13_out, not_14_out, not_15_out, not_16_out, not_17_out,
       not_18_out, not_19_out, not_20_out, not_21_out, not_22_out, not_23_out, not_24_out, not_25_out,
       not_26_out, not_27_out, not_28_out, not_29_out, or_2_out, or_3_out, or_4_out, or_5_out, or_6_out,
       or_10_out;

  not not_1 (not_1_out, A);
  not not_2 (not_2_out, B);
  not not_3 (not_3_out, C);
  not not_4 (not_4_out, A);
  not not_5 (not_5_out, B);
  not not_6 (not_6_out, A);
  not not_7 (not_7_out, B);
  not not_8 (not_8_out, B);
  not not_9 (not_9_out, A);
  not not_10 (not_10_out, B);
  not not_11 (not_11_out, B);
  not not_12 (not_12_out, C);
  not not_13 (not_13_out, A);
  not not_14 (not_14_out, A);
  not not_15 (not_15_out, B);
  not not_16 (not_16_out, A);
  not not_17 (not_17_out, B);
  not not_18 (not_18_out, A);
  not not_19 (not_19_out, A);
  not not_20 (not_20_out, B);
  not not_21 (not_21_out, B);
  not not_22 (not_22_out, C);
  and and_1 (and_1_out, not_1_out, not_2_out);
  and and_2 (and_2_out, A, not_3_out);
  and and_3 (and_3_out, not_4_out, not_5_out);
  not not_23 (not_23_out, C);
  and and_4 (and_4_out, not_6_out, not_7_out);
  and and_5 (and_5_out, not_8_out, C);
  and and_6 (and_6_out, not_9_out, not_10_out);
  and and_7 (and_7_out, not_11_out, not_12_out);
  not not_24 (not_24_out, A);
  and and_8 (and_8_out, not_13_out, C);
  and and_9 (and_9_out, not_14_out, B);
  and and_10 (and_10_out, A, not_15_out);
  not not_25 (not_25_out, C);
  and and_11 (and_11_out, not_16_out, not_17_out);
  and and_12 (and_12_out, not_18_out, B);
  not not_26 (not_26_out, C);
  not not_27 (not_27_out, B);
  and and_13 (and_13_out, not_19_out, not_20_out);
  and and_14 (and_14_out, not_21_out, not_22_out);
  not not_28 (not_28_out, A);
  or or_1 (a_2, and_1_out, and_2_out);
  and and_15 (and_15_out, and_3_out, not_23_out);
  and and_16 (and_16_out, A, C);
  or or_2 (or_2_out, and_4_out, and_5_out);
  and and_17 (and_17_out, A, B);
  or or_3 (or_3_out, and_6_out, and_7_out);
  and and_18 (and_18_out, not_24_out, C);
  or or_4 (or_4_out, and_8_out, and_9_out);
  and and_19 (and_19_out, and_10_out, not_25_out);
  and and_20 (and_20_out, and_11_out, C);
  and and_21 (and_21_out, and_12_out, not_26_out);
  and and_22 (and_22_out, A, not_27_out);
  not not_29 (not_29_out, C);
  or or_5 (or_5_out, and_13_out, and_14_out);
  and and_23 (and_23_out, not_28_out, C);
  or or_6 (or_6_out, and_15_out, and_16_out);
  and and_24 (and_24_out, A, B);
  or or_7 (c_2, or_2_out, and_17_out);
  or or_8 (d, or_3_out, and_18_out);
  or or_9 (e, or_4_out, and_19_out);
  or or_10 (or_10_out, and_20_out, and_21_out);
  and and_25 (and_25_out, and_22_out, not_29_out);
  or or_11 (g, or_5_out, and_23_out);
  or or_12 (b_2, or_6_out, and_24_out);
  or or_13 (f, or_10_out, and_25_out);
  _7_Segment_Display u_7_segment_display_1 (.g(g), .f(f), .a(a_2), .b(b_2), .e(e), .d(d), .c(c_2));  // open: dp
endmodule

module SOP (
  input  A,
  input  B,
  input  C,
  output a_2,
  output b_2,
  output c_2,
  output d,
  output e,
  output f,
  output f_2
);

  wire and_1_out, and_2_out, and_3_out, and_4_out, and_5_out, and_6_out, and_7_out, and_8_out, and_9_out,
       and_10_out, and_11_out, and_12_out, and_13_out, and_14_out, and_15_out, and_16_out, and_17_out,
       and_18_out, and_19_out, and_20_out, and_21_out, and_22_out, and_23_out, and_24_out, not_1_out,
       not_2_out, not_3_out, or_1_out, or_2_out, or_3_out, or_4_out, or_5_out, or_6_out, or_7_out;

  not not_1 (not_1_out, A);
  not not_2 (not_2_out, B);
  not not_3 (not_3_out, C);
  or or_1 (or_1_out, not_1_out, not_3_out);
  and and_1 (and_1_out, not_1_out, not_3_out);
  and and_2 (and_2_out, A, C);
  and and_3 (and_3_out, A, B);
  and and_4 (and_4_out, not_1_out, not_2_out);
  and and_5 (and_5_out, not_2_out, C);
  and and_6 (and_6_out, A, B);
  and and_7 (and_7_out, not_1_out, not_2_out);
  and and_8 (and_8_out, not_2_out, not_3_out);
  and and_9 (and_9_out, not_1_out, C);
  or or_2 (or_2_out, B, C);
  and and_10 (and_10_out, not_2_out, A);
  and and_11 (and_11_out, not_2_out, C);
  and and_12 (and_12_out, B, not_3_out);
  and and_13 (and_13_out, A, not_2_out);
  and and_14 (and_14_out, not_1_out, C);
  or or_3 (or_3_out, not_1_out, not_3_out);
  and and_15 (and_15_out, or_1_out, not_2_out);
  and and_16 (and_16_out, not_3_out, A);
  or or_4 (or_4_out, and_1_out, and_2_out);
  and and_17 (and_17_out, and_3_out, not_3_out);
  or or_5 (or_5_out, and_4_out, and_5_out);
  and and_18 (and_18_out, and_6_out, C);
  or or_6 (or_6_out, and_7_out, and_8_out);
  and and_19 (and_19_out, or_2_out, not_1_out);
  and and_20 (and_20_out, and_10_out, not_3_out);
  or or_7 (or_7_out, and_11_out, and_12_out);
  and and_21 (and_21_out, and_13_out, not_3_out);
  and and_22 (and_22_out, or_3_out, not_2_out);
  and and_23 (and_23_out, or_4_out, not_2_out);
  and and_24 (and_24_out, or_7_out, not_1_out);
  or or_8 (a_2, and_15_out, and_16_out);
  or or_9 (c_2, or_5_out, and_18_out);
  or or_10 (d, or_6_out, and_9_out);
  or or_11 (e, and_19_out, and_20_out);
  or or_12 (f, and_24_out, and_21_out);
  or or_13 (f_2, and_14_out, and_22_out);
  or or_14 (b_2, and_23_out, and_17_out);
  _7_Segment_Display u_7_segment_display_1 (.g(f_2), .f(f), .a(a_2), .b(b_2), .e(e), .d(d), .c(c_2));  // open: dp
endmodule

module POS (
  input  A,
  input  B,
  input  C,
  output a_2,
  output b_2,
  output c_2,
  output d,
  output e,
  output f,
  output g
);

  wire and_1_out, and_2_out, and_3_out, and_4_out, and_5_out, and_6_out, and_7_out, and_8_out, and_9_out,
       and_10_out, and_11_out, and_12_out, and_13_out, and_14_out, and_15_out, and_16_out, and_17_out,
       and_18_out, and_19_out, and_20_out, and_21_out, not_1_out, not_2_out, not_3_out, or_1_out, or_2_out,
       or_3_out, or_4_out, or_5_out, or_6_out, or_7_out, or_8_out, or_9_out, or_10_out, or_11_out, or_12_out,
       or_17_out;

  not not_1 (not_1_out, A);
  not not_2 (not_2_out, B);
  not not_3 (not_3_out, C);
  or or_1 (or_1_out, B, not_3_out);
  or or_2 (or_2_out, not_1_out, not_3_out);
  or or_3 (or_3_out, B, C);
  and and_1 (and_1_out, not_1_out, not_2_out);
  or or_4 (or_4_out, B, C);
  or or_5 (or_5_out, not_1_out, C);
  or or_6 (or_6_out, not_1_out, not_3_out);
  or or_7 (or_7_out, not_1_out, B);
  or or_8 (or_8_out, B, C);
  and and_2 (and_2_out, A, not_2_out);
  and and_3 (and_3_out, B, C);
  and and_4 (and_4_out, not_2_out, not_3_out);
  and and_5 (and_5_out, B, not_3_out);
  and and_6 (and_6_out, not_2_out, C);
  or or_9 (or_9_out, not_1_out, not_3_out);
  or or_10 (or_10_out, not_1_out, B);
  and and_7 (and_7_out, or_1_out, A);
  and and_8 (and_8_out, or_2_out, not_2_out);
  and and_9 (and_9_out, or_3_out, A);
  and and_10 (and_10_out, and_1_out, not_3_out);
  and and_11 (and_11_out, or_4_out, A);
  and and_12 (and_12_out, or_5_out, not_2_out);
  and and_13 (and_13_out, or_6_out, not_2_out);
  and and_14 (and_14_out, or_7_out, C);
  and and_15 (and_15_out, or_8_out, not_1_out);
  and and_16 (and_16_out, B, C);
  and and_17 (and_17_out, and_2_out, not_3_out);
  or or_11 (or_11_out, and_3_out, and_4_out);
  or or_12 (or_12_out, and_5_out, and_6_out);
  and and_18 (and_18_out, or_9_out, not_2_out);
  and and_19 (and_19_out, or_10_out, C);
  and and_20 (and_20_out, or_11_out, A);
  and and_21 (and_21_out, or_12_out, not_1_out);
  or or_13 (a_2, and_7_out, and_8_out);
  or or_14 (b_2, and_9_out, and_10_out);
  or or_15 (c_2, and_11_out, and_12_out);
  or or_16 (d, and_13_out, and_14_out);
  or or_17 (or_17_out, and_15_out, and_16_out);
  or or_18 (e, or_17_out, and_17_out);
  or or_19 (f, and_20_out, and_21_out);
  or or_20 (g, and_18_out, and_19_out);
  _7_Segment_Display u_7_segment_display_1 (.g(g), .f(f), .a(a_2), .b(b_2), .e(e), .d(d), .c(c_2));  // open: dp
endmodule
